# Fritzing sketch circuits (saved by Fritzing 0.9.3b)
breadboards: 2

parts:
  Componente1 = Arduino Uno (Rev3)
  hc-sr1 = hc-sr04
  Componente2 = Arduino Uno (Rev3)
  hc-sr2 = hc-sr04
  M1 = DC Motor

nets:
  N1: Componente1.D6_PWM, hc-sr1.Trig
  N2: Componente1.D7, hc-sr1.Echo
  5V: Componente1.5V, hc-sr1.VCC
  GND: Componente1.GND, hc-sr1.GND
  N3: Componente2.D8, M1.pin_2
  N4: Componente2.D6_PWM, hc-sr2.Trig
  N5: Componente2.D7, hc-sr2.Echo
  5V_2: Componente2.5V, hc-sr2.VCC
  GND_2: Componente2.GND, hc-sr2.GND

notes:
  SensorUltrasound
  SensorUltrasomComMotor
